# Fritzing sketch RPi.Relay (saved by Fritzing 0.9.2b)

parts:
  Raspberry_Pi_B_rev1 = Raspberry Pi B rev1
  KY-1 = Keyes Relay [package=THT]

nets:
  N1: Raspberry_Pi_B_rev1.5V, KY-1.power
  N2: Raspberry_Pi_B_rev1.GND, KY-1.ground
  N3: Raspberry_Pi_B_rev1.GPIO_22, KY-1.signal

custom parts:
  Keyes Relay: The Keyes 5V relay module is suitable for SCM development, home appliance control. It uses a 5V~12V TIL control signal which can control DC / AC signal.
